// Logisim project mipsjal.circ as structural Verilog
module main (
  input  in_1
);

  wire alucontrol_1_isbyte, alucontrol_1_isjumpreg, alucontrol_1_isslt, aluzero_1_zero, branch_1_decision,
       clock_1_out, control_1_alusrc, control_1_branch, control_1_jump, control_1_memread,
       control_1_memwrite, control_1_regwrite, luicheck_1_lui, or_1_out, unsignedchecker_1_isunsigned;
  wire [0:0] comparator_1_lt;
  wire [1:0] control_1_memtoreg, control_1_regdest, multiplexer_6_out;
  wire [3:0] alucontrol_1_aluopcode, control_1_aluop, multiplexer_10_out, shifter_3_out;
  wire [4:0] multiplexer_3_out, shamt_1_shamt;
  wire [29:0] incrementer_1_p2, multiplexer_1_out, multiplexer_6_out_2, register_1_q;
  wire [31:0] adder_1_out, bit_extender_1_out, loadshifter_1_out_5, mips_alu_1_p5, mips_ram_1_p7,
       mipsprogramrom_1_p1, multiplexer_2_out, multiplexer_4_out, multiplexer_5_out, multiplexer_7_out,
       multiplexer_8_out, multiplexer_9_out, registerfile_1_p1, registerfile_1_p7, registerfile_1_p8,
       shifter_1_out, shifter_2_out;

  Clock clock_1 (.out(clock_1_out));
  Multiplexer #(.width(30), .enable("false")) multiplexer_1 (
    .in0(incrementer_1_p2), .in1(multiplexer_6_out_2), .out(multiplexer_1_out), .sel(or_1_out));
  Register #(.width(30)) register_1 (
    .D(multiplexer_1_out), .clk(clock_1_out), .Q(register_1_q), .clr(in_1));  // open: en
  or or_1 (or_1_out, control_1_jump, alucontrol_1_isjumpreg, control_1_branch);
  // Incrementer #(.width(30)) incrementer_1: pin names not known; wires that end beside it: register_1_q, incrementer_1_p2, {register_1_q, 2'b00}
  // MIPSProgramROM mipsprogramrom_1: pin names not known; wires that end beside it: mipsprogramrom_1_p1
  Shifter #(.width(32)) shifter_1 (.in(multiplexer_5_out), .\dist (5'b00010), .out(shifter_1_out));
  Control control_1 (
    .OpCode(mipsprogramrom_1_p1[31:26]), .RegDest(control_1_regdest), .Jump(control_1_jump),
    .ALUSrc(control_1_alusrc), .MemtoReg(control_1_memtoreg), .RegWrite(control_1_regwrite),
    .MemRead(control_1_memread), .MemWrite(control_1_memwrite), .Branch(control_1_branch),
    .ALUOp(control_1_aluop));
  Adder #(.width(32)) adder_1 (.a({incrementer_1_p2, 2'b00}), .b(shifter_1_out), .out(adder_1_out));  // open: cin, cout
  Multiplexer #(.width(32), .enable("false")) multiplexer_2 (
    .in0({incrementer_1_p2, 2'b00}), .in1(adder_1_out), .out(multiplexer_2_out), .sel(branch_1_decision));
  Multiplexer #(.select(2), .width(5), .enable("false")) multiplexer_3 (
    .in0(mipsprogramrom_1_p1[20:16]), .in1(mipsprogramrom_1_p1[15:11]), .in2({5{1'b1}}),
    .out(multiplexer_3_out), .sel(control_1_regdest));  // open: in3
  assign bit_extender_1_out = {{16{mipsprogramrom_1_p1[15]}}, mipsprogramrom_1_p1[15:0]};  // Bit_Extender bit_extender_1
  LUICheck luicheck_1 (.in_1(mipsprogramrom_1_p1[31:26]), .LUI(luicheck_1_lui));
  Multiplexer #(.width(32), .enable("false")) multiplexer_4 (
    .in0(multiplexer_2_out), .in1({incrementer_1_p2[29:26], mipsprogramrom_1_p1[25:0], 2'b00}),
    .out(multiplexer_4_out), .sel(control_1_jump));
  // RegisterFile registerfile_1: pin names not known; wires that end beside it: registerfile_1_p1, clock_1_out, control_1_regwrite, multiplexer_3_out, mipsprogramrom_1_p1[25:21], mipsprogramrom_1_p1[20:16], registerfile_1_p7, registerfile_1_p8
  Shifter #(.width(32)) shifter_2 (.in(bit_extender_1_out), .\dist (5'b10000), .out(shifter_2_out));
  Multiplexer #(.width(32), .enable("false")) multiplexer_5 (
    .in0(bit_extender_1_out), .in1(shifter_2_out), .out(multiplexer_5_out), .sel(luicheck_1_lui));
  ALUControl alucontrol_1 (
    .Op(control_1_aluop), .Instruction(mipsprogramrom_1_p1[5:0]), .ALUOpCode(alucontrol_1_aluopcode),
    .IsByte(alucontrol_1_isbyte), .IsSLT(alucontrol_1_isslt), .IsJumpReg(alucontrol_1_isjumpreg));
  Shamt shamt_1 (
    .CodeConstant(mipsprogramrom_1_p1[15:0]), .RegA(registerfile_1_p7),
    .Instruction(mipsprogramrom_1_p1[5:0]), .Shamt(shamt_1_shamt));
  Multiplexer #(.width(32), .enable("false")) multiplexer_6 (
    .in0(multiplexer_4_out), .in1(registerfile_1_p7), .out({multiplexer_6_out_2, multiplexer_6_out}),
    .sel(alucontrol_1_isjumpreg));
  Multiplexer #(.width(32), .enable("false")) multiplexer_7 (
    .in0(registerfile_1_p8), .in1(multiplexer_5_out), .out(multiplexer_7_out), .sel(control_1_alusrc));
  // Mips_ALU mips_alu_1: pin names not known; wires that end beside it: registerfile_1_p7, multiplexer_7_out, alucontrol_1_aluopcode, shamt_1_shamt, mips_alu_1_p5
  Comparator #(.width(32)) comparator_1 (
    .a(registerfile_1_p7), .b(multiplexer_7_out), .lt(comparator_1_lt[0]));  // open: gt, eq
  Comparator #(.width(32), .mode("unsigned")) comparator_2 (
    .a(registerfile_1_p7), .b(multiplexer_7_out));  // open: gt, eq, lt
  ALUZero aluzero_1 (.A(registerfile_1_p7), .B(registerfile_1_p8), .Zero(aluzero_1_zero));
  Multiplexer #(.width(32), .enable("false")) multiplexer_8 (
    .in0(mips_alu_1_p5), .in1({{31{1'b0}}, comparator_1_lt[0]}), .out(multiplexer_8_out),
    .sel(alucontrol_1_isslt));
  Multiplexer #(.width(32), .enable("false")) multiplexer_9 (
    .in0(registerfile_1_p8),
    .in1({registerfile_1_p8[7:0], registerfile_1_p8[7:0], registerfile_1_p8[7:0], registerfile_1_p8[7:0]}),
    .out(multiplexer_9_out), .sel(alucontrol_1_isbyte));
  Multiplexer #(.width(4), .enable("false")) multiplexer_10 (
    .in0(4'b1111), .in1(shifter_3_out), .out(multiplexer_10_out), .sel(alucontrol_1_isbyte));
  Shifter #(.width(4)) shifter_3 (.in(4'b0001), .\dist (multiplexer_8_out[1:0]), .out(shifter_3_out));
  UnsignedChecker unsignedchecker_1 (.OpCode(mipsprogramrom_1_p1[31:26]), .IsUnsigned(unsignedchecker_1_isunsigned));
  Branch branch_1 (
    .Branch(control_1_branch), .Zero(aluzero_1_zero), .ALUOp2(control_1_aluop[1]),
    .Decision(branch_1_decision));
  // MIPS_RAM #(.addrWidth(24)) mips_ram_1: pin names not known; wires that end beside it: multiplexer_8_out[25:2], multiplexer_9_out, control_1_memwrite, multiplexer_10_out, clock_1_out, control_1_memread, mips_ram_1_p7
  LoadShifter loadshifter_1 (
    .ValueIn(mips_ram_1_p7), .Cin(multiplexer_8_out), .IsUnsigned(unsignedchecker_1_isunsigned),
    .IsByte(alucontrol_1_isbyte), .out_5(loadshifter_1_out_5));
  Multiplexer #(.select(2), .width(32), .enable("false")) multiplexer_11 (
    .in0(multiplexer_8_out), .in1(loadshifter_1_out_5), .in2({incrementer_1_p2, 2'b00}),
    .out(registerfile_1_p1), .sel(control_1_memtoreg));  // open: in3

  // Notes on the sheet:
  //   contents of mipsprogramrom_1 (hex, n*v repeats v):
  //   ori     $8, $0, 52345     sw      $8, 4($0)     sb      $8, 8($0)     sb      $8, 10($0)     lw
  //   $9, 4($0)     lb      $10, 10($0)     lui     $11, 52345
endmodule

module ALUControlLogic (
  input  Op3,
  input  Op2,
  input  Op1,
  input  Op0,
  input  Fn5,
  input  Fn4,
  input  Fn3,
  input  Fn2,
  input  Fn1,
  input  Fn0,
  output OpCode3,
  output OpCode2,
  output OpCode1,
  output OpCode0,
  output IsByte,
  output IsSLT,
  output IsJumpReg
);

  wire nor_1_out, not_1_out, not_2_out, not_3_out;
  wire [3:0] opcodealucontrol_1_opcode0, ralucontrol_1_out_10;

  nor nor_1 (nor_1_out, Op3, Op2, Op1, Op0);
  not not_1 (not_1_out, Fn4);
  not not_2 (not_2_out, Fn2);
  not not_3 (not_3_out, Fn3);
  OpCodeALUControl opcodealucontrol_1 (
    .Op3(Op3), .Op2(Op2), .Op1(Op1), .Op0(Op0), .OpCode3(opcodealucontrol_1_opcode0[3]),
    .OpCode2(opcodealucontrol_1_opcode0[2]), .OpCode1(opcodealucontrol_1_opcode0[1]),
    .OpCode0(opcodealucontrol_1_opcode0[0]));
  IsByteALUControl isbytealucontrol_1 (.Op3(Op3), .Op2(Op2), .Op1(Op1), .Op0(Op0), .IsByte(IsByte));
  and and_1 (IsSLT, Fn5, not_1_out, Fn3, not_2_out, Fn1);
  nor nor_2 (IsJumpReg, Fn5, Fn4, not_3_out, Op0, Fn2, Fn1, Fn0);
  RALUControl ralucontrol_1 (
    .F5(Fn5), .F4(Fn4), .F3(Fn3), .F2(Fn2), .F1(Fn1), .F0(Fn0), .out_7(ralucontrol_1_out_10[3]),
    .out_8(ralucontrol_1_out_10[2]), .out_9(ralucontrol_1_out_10[1]), .out_10(ralucontrol_1_out_10[0]));
  Multiplexer #(.width(4), .enable("false")) multiplexer_1 (
    .in0(opcodealucontrol_1_opcode0), .in1(ralucontrol_1_out_10), .out({OpCode3, OpCode2, OpCode1, OpCode0}),
    .sel(nor_1_out));
endmodule

module ALUControl (
  input  [3:0] Op,
  input  [5:0] Instruction,
  output [3:0] ALUOpCode,
  output IsByte,
  output IsSLT,
  output IsJumpReg
);

  ALUControlLogic alucontrollogic_1 (
    .Op3(Op[0]), .Op2(Op[1]), .Op1(Op[2]), .Op0(Op[3]), .Fn5(Instruction[5]), .Fn4(Instruction[4]),
    .Fn3(Instruction[3]), .Fn2(Instruction[2]), .Fn1(Instruction[1]), .Fn0(Instruction[0]),
    .OpCode3(ALUOpCode[3]), .OpCode2(ALUOpCode[2]), .OpCode1(ALUOpCode[1]), .OpCode0(ALUOpCode[0]),
    .IsByte(IsByte), .IsSLT(IsSLT), .IsJumpReg(IsJumpReg));
endmodule

module ControlLogic (
  input  Op5,
  input  Op4,
  input  Op3,
  input  Op2,
  input  Op1,
  input  Op0,
  output Jump,
  output ALUSrc,
  output RegWrite,
  output MemRead,
  output MemWrite,
  output Branch,
  output AluOp3,
  output AluOp2,
  output AluOp1,
  output AluOp0
);

  wire and_3_out, and_4_out, and_5_out, and_6_out, and_10_out, and_11_out, and_12_out, and_13_out,
       and_14_out, and_15_out, and_16_out, and_17_out, and_18_out, and_19_out, not_1_out, not_2_out,
       not_3_out, not_4_out, not_5_out, not_6_out, not_7_out, not_8_out, not_9_out, not_10_out, not_11_out,
       not_12_out, not_13_out, not_14_out, not_15_out, not_16_out, not_17_out, not_18_out, not_19_out,
       not_20_out, not_21_out, not_22_out, not_23_out, not_24_out, not_25_out, not_26_out;

  not not_1 (not_1_out, Op5);
  not not_2 (not_2_out, Op3);
  or or_1 (ALUSrc, Op3, Op5);
  not not_3 (not_3_out, Op3);
  not not_4 (not_4_out, Op2);
  not not_5 (not_5_out, Op1);
  not not_6 (not_6_out, Op3);
  not not_7 (not_7_out, Op2);
  not not_8 (not_8_out, Op5);
  not not_9 (not_9_out, Op3);
  not not_10 (not_10_out, Op3);
  and and_1 (MemWrite, Op5, Op3);
  not not_11 (not_11_out, Op5);
  not not_12 (not_12_out, Op3);
  not not_13 (not_13_out, Op0);
  not not_14 (not_14_out, Op3);
  not not_15 (not_15_out, Op1);
  not not_16 (not_16_out, Op5);
  not not_17 (not_17_out, Op2);
  not not_18 (not_18_out, Op1);
  not not_19 (not_19_out, Op5);
  not not_20 (not_20_out, Op2);
  not not_21 (not_21_out, Op1);
  not not_22 (not_22_out, Op1);
  not not_23 (not_23_out, Op3);
  not not_24 (not_24_out, Op3);
  not not_25 (not_25_out, Op2);
  not not_26 (not_26_out, Op0);
  and and_2 (Jump, not_1_out, not_2_out, Op1);
  and and_3 (and_3_out, not_3_out, not_4_out, not_5_out);
  and and_4 (and_4_out, not_6_out, not_7_out, Op0);
  and and_5 (and_5_out, not_8_out, Op3);
  and and_6 (and_6_out, Op5, not_9_out);
  and and_7 (MemRead, Op5, not_10_out);
  and and_8 (Branch, not_11_out, not_12_out, Op2);
  and and_9 (AluOp3, Op2, Op1, not_13_out);
  and and_10 (and_10_out, not_14_out, not_15_out, Op0);
  and and_11 (and_11_out, not_16_out, Op3, not_17_out, Op1);
  and and_12 (and_12_out, Op5, not_18_out);
  and and_13 (and_13_out, not_19_out, Op3, not_20_out, Op1);
  and and_14 (and_14_out, Op3, Op2, not_21_out);
  and and_15 (and_15_out, not_22_out, Op0);
  and and_16 (and_16_out, not_23_out, Op1);
  and and_17 (and_17_out, not_24_out, Op2);
  and and_18 (and_18_out, Op2, Op0);
  and and_19 (and_19_out, Op3, not_25_out, not_26_out);
  or or_2 (RegWrite, and_3_out, and_4_out, and_5_out, and_6_out);
  or or_3 (AluOp2, and_10_out, and_11_out, and_12_out);
  or or_4 (AluOp1, and_13_out, and_14_out);
  or or_5 (AluOp0, and_15_out, and_16_out, and_17_out, and_18_out, and_19_out, Op5);
endmodule

module Control (
  input  [5:0] OpCode,
  output [1:0] RegDest,
  output Jump,
  output ALUSrc,
  output [1:0] MemtoReg,
  output RegWrite,
  output MemRead,
  output MemWrite,
  output Branch,
  output [3:0] ALUOp
);

  ControlLogic controllogic_1 (
    .Op5(OpCode[5]), .Op4(OpCode[4]), .Op3(OpCode[3]), .Op2(OpCode[2]), .Op1(OpCode[1]), .Op0(OpCode[0]),
    .Jump(Jump), .ALUSrc(ALUSrc), .RegWrite(RegWrite), .MemRead(MemRead), .MemWrite(MemWrite),
    .Branch(Branch), .AluOp3(ALUOp[0]), .AluOp2(ALUOp[1]), .AluOp1(ALUOp[2]), .AluOp0(ALUOp[3]));
  ControlRegDestMemtoReg controlregdestmemtoreg_1 (
    .Op5(OpCode[5]), .Op4(OpCode[4]), .Op3(OpCode[3]), .Op2(OpCode[2]), .Op1(OpCode[1]), .Op0(OpCode[0]),
    .RegDest1(RegDest[1]), .RegDest0(RegDest[0]), .MemtoReg1(MemtoReg[1]), .MemtoReg0(MemtoReg[0]));
endmodule

module OpCodeALUControl (
  input  Op3,
  input  Op2,
  input  Op1,
  input  Op0,
  output OpCode3,
  output OpCode2,
  output OpCode1,
  output OpCode0
);

  wire and_1_out, and_2_out, and_4_out, and_5_out, not_1_out, not_2_out, not_3_out, not_4_out, not_5_out,
       not_6_out, not_7_out;

  not not_1 (not_1_out, Op1);
  and and_1 (and_1_out, not_1_out, not_2_out);
  not not_2 (not_2_out, Op0);
  not not_3 (not_3_out, Op2);
  and and_2 (and_2_out, not_3_out, Op1);
  not not_4 (not_4_out, Op1);
  and and_3 (OpCode2, not_4_out, not_5_out);
  not not_5 (not_5_out, Op0);
  not not_6 (not_6_out, Op2);
  and and_4 (and_4_out, not_6_out, Op0);
  not not_7 (not_7_out, Op1);
  and and_5 (and_5_out, not_7_out, Op0);
  or or_1 (OpCode3, and_1_out, and_2_out);
  or or_2 (OpCode1, and_4_out, and_5_out);

  assign OpCode0 = 1'b0;
endmodule

module RALUControl (
  input  F5,
  input  F4,
  input  F3,
  input  F2,
  input  F1,
  input  F0,
  output out_7,
  output out_8,
  output out_9,
  output out_10
);

  wire and_1_out, and_2_out, and_3_out, and_4_out, not_1_out, not_2_out, not_3_out, not_4_out;

  and and_1 (and_1_out, F5, F2);
  not not_1 (not_1_out, F3);
  not not_2 (not_2_out, F2);
  not not_3 (not_3_out, F3);
  not not_4 (not_4_out, F5);
  or or_1 (out_7, F3, and_1_out);
  and and_2 (and_2_out, F5, not_1_out, not_2_out);
  and and_3 (and_3_out, F5, not_3_out, F0);
  and and_4 (and_4_out, not_4_out, F0);
  or or_2 (out_9, and_2_out, and_3_out);
  or or_3 (out_10, and_4_out, F3);

  assign out_8 = F1;
endmodule

module ALUZero (
  input  [31:0] A,
  input  [31:0] B,
  output Zero
);

  Comparator #(.width(32)) comparator_1 (.a(A), .b(B), .eq(Zero));  // open: gt, lt
endmodule

module Branch (
  input  Branch,
  input  Zero,
  input  ALUOp2,
  output Decision
);

  wire and_1_out, and_2_out, not_1_out, not_2_out;

  not not_1 (not_1_out, Zero);
  not not_2 (not_2_out, ALUOp2);
  and and_1 (and_1_out, not_1_out, Branch, ALUOp2);
  and and_2 (and_2_out, Zero, Branch, not_2_out);
  or or_1 (Decision, and_1_out, and_2_out);
endmodule

module IsByteALUControl (
  input  Op3,
  input  Op2,
  input  Op1,
  input  Op0,
  output IsByte
);


  assign IsByte = Op2;
endmodule

module LoadShifter (
  input  [31:0] ValueIn,
  input  [31:0] Cin,
  input  IsUnsigned,
  input  IsByte,
  output [31:0] out_5
);

  wire [4:0] shifter_1_out;
  wire [31:0] bit_extender_1_out, bit_extender_2_out, multiplexer_1_out, shifter_2_out;

  Shifter #(.width(5)) shifter_1 (.in({3'b000, Cin[1:0]}), .\dist (3'b011), .out(shifter_1_out));
  Shifter #(.width(32), .shift("ar")) shifter_2 (.in(ValueIn), .\dist (shifter_1_out), .out(shifter_2_out));
  assign bit_extender_1_out = {{24{shifter_2_out[7]}}, shifter_2_out[7:0]};  // Bit_Extender bit_extender_1
  Multiplexer #(.width(32), .enable("false")) multiplexer_1 (
    .in0(bit_extender_1_out), .in1(bit_extender_2_out), .out(multiplexer_1_out), .sel(IsUnsigned));
  assign bit_extender_2_out = {{24{1'b0}}, shifter_2_out[7:0]};  // Bit_Extender bit_extender_2
  Multiplexer #(.width(32), .enable("false")) multiplexer_2 (
    .in0(ValueIn), .in1(multiplexer_1_out), .out(out_5), .sel(IsByte));
endmodule

module UnsignedChecker (
  input  [5:0] OpCode,
  output IsUnsigned
);

  UnsignedCheckerLogic unsignedcheckerlogic_1 (
    .Op5(OpCode[5]), .Op4(OpCode[4]), .Op3(OpCode[3]), .Op2(OpCode[2]), .Op1(OpCode[1]), .Op0(OpCode[0]),
    .IsUnsigned(IsUnsigned));
endmodule

module UnsignedCheckerLogic (
  input  Op5,
  input  Op4,
  input  Op3,
  input  Op2,
  input  Op1,
  input  Op0,
  output IsUnsigned
);

  wire and_1_out, and_2_out, not_1_out, not_2_out, not_3_out, not_4_out, not_5_out, not_6_out, not_7_out;

  not not_1 (not_1_out, Op5);
  not not_2 (not_2_out, Op4);
  not not_3 (not_3_out, Op2);
  not not_4 (not_4_out, Op4);
  not not_5 (not_5_out, Op3);
  not not_6 (not_6_out, Op1);
  not not_7 (not_7_out, Op0);
  and and_1 (and_1_out, not_1_out, not_2_out, Op3, not_3_out, Op1, Op0);
  and and_2 (and_2_out, Op5, not_4_out, not_5_out, Op2, not_6_out, not_7_out);
  or or_1 (IsUnsigned, and_1_out, and_2_out);
endmodule

module Shamt (
  input  [15:0] CodeConstant,
  input  [31:0] RegA,
  input  [5:0] Instruction,
  output [4:0] Shamt
);

  wire shamtlogic_1_shiftfromregister;

  Multiplexer #(.width(5), .enable("false")) multiplexer_1 (
    .in0(CodeConstant[10:6]), .in1(RegA[4:0]), .out(Shamt), .sel(shamtlogic_1_shiftfromregister));
  ShamtLogic shamtlogic_1 (
    .Fn5(Instruction[5]), .Fn4(Instruction[4]), .Fn3(Instruction[3]), .Fn2(Instruction[2]),
    .Fn1(Instruction[1]), .Fn0(Instruction[0]), .ShiftFromRegister(shamtlogic_1_shiftfromregister));
endmodule

module ShamtLogic (
  input  Fn5,
  input  Fn4,
  input  Fn3,
  input  Fn2,
  input  Fn1,
  input  Fn0,
  output ShiftFromRegister
);


  assign ShiftFromRegister = Fn2;
endmodule

module ControlRegDestMemtoReg (
  input  Op5,
  input  Op4,
  input  Op3,
  input  Op2,
  input  Op1,
  input  Op0,
  output RegDest1,
  output RegDest0,
  output MemtoReg1,
  output MemtoReg0
);

  wire not_1_out, not_2_out, not_3_out, not_4_out, not_5_out, not_6_out, not_7_out, not_8_out, not_9_out,
       not_10_out, not_11_out;

  not not_1 (not_1_out, Op5);
  not not_2 (not_2_out, Op3);
  not not_3 (not_3_out, Op2);
  not not_4 (not_4_out, Op5);
  not not_5 (not_5_out, Op3);
  not not_6 (not_6_out, Op2);
  not not_7 (not_7_out, Op1);
  not not_8 (not_8_out, Op5);
  not not_9 (not_9_out, Op3);
  not not_10 (not_10_out, Op2);
  not not_11 (not_11_out, Op3);
  and and_1 (RegDest1, not_1_out, not_2_out, not_3_out, Op0);
  and and_2 (RegDest0, not_4_out, not_5_out, not_6_out, not_7_out);
  and and_3 (MemtoReg1, not_8_out, not_9_out, not_10_out, Op0);
  and and_4 (MemtoReg0, Op5, not_11_out);
endmodule

module LUICheckLogic (
  input  Op5,
  input  Op4,
  input  Op3,
  input  Op2,
  input  Op1,
  input  Op0,
  output LUI
);

  wire not_1_out, not_2_out;

  not not_1 (not_1_out, Op5);
  not not_2 (not_2_out, Op4);
  and and_1 (LUI, not_1_out, not_2_out, Op3, Op2, Op1, Op0);
endmodule

module LUICheck (
  input  [5:0] in_1,
  output LUI
);

  LUICheckLogic luichecklogic_1 (
    .Op5(in_1[5]), .Op4(in_1[4]), .Op3(in_1[3]), .Op2(in_1[2]), .Op1(in_1[1]), .Op0(in_1[0]), .LUI(LUI));
endmodule
